// Logisim project Basic4Bit.circ as structural Verilog: 1 circuit, main circuit main
module main (
  input  in_1,
  input  [7:0] in_2
);

  wire A, A_pin7, A_pin9, A_pin10, ADD, adder_1_cout, and_1_out, and_2_out, and_3_out, and_4_out, and_5_out,
       and_6_out, and_7_out, B_pin7, B_pin9, B_pin10, C_q, CLK, CMP, FD, instNAND, JPC, JPZ, LDI, LDST,
       n74138_1_pin4, n74138_1_pin5, n74138_1_pin6, nand_1_out, nCLK, not_3_out, not_4_out, not_5_out,
       not_6_out, not_8_out, not_9_out, nRESET, PCH_pin2, PCH_pin7, PCH_pin9, PCH_pin10, PCL_pin7, PCL_pin9,
       PCL_pin10, PT, ST, TEMP_pin1, TEMP_pin7, TEMP_pin9, TEMP_pin10;
  wire [3:0] adder_1_out, AOUT, BOUT, controlled_buffer_3_out, controlled_buffer_8_out,
       controlled_buffer_9_out, controlled_buffer_10_out, DATA, nand_2_out, PCH_pin14, PCL_pin14, TEMPOUT,
       undriven;
  wire [3:3] pull_resistor_1_node;
  wire [7:0] ADDRESS, PCH_pin3;

  Clock clock_1 (.out(CLK));
  // DipSwitch Start: pin names not known
  not not_1 (nRESET, in_1);
  not not_2 (nCLK, CLK);
  _74161 #(.ShowInternalStructure("true")) PCH (
    .pin1(nRESET), .pin2(PCH_pin2), .pin3(PCH_pin3[0]), .pin4(PCH_pin3[1]), .pin5(PCH_pin3[2]),
    .pin6(PCH_pin3[3]), .pin7(PCH_pin7), .pin14(PCH_pin14[0]), .pin13(PCH_pin14[1]), .pin12(PCH_pin14[2]),
    .pin11(PCH_pin14[3]), .pin10(PCH_pin10), .pin9(PCH_pin9));  // open: pin15
  _74161 #(.ShowInternalStructure("true")) PCL (
    .pin1(nRESET), .pin2(nCLK), .pin3(PCH_pin3[4]), .pin4(PCH_pin3[5]), .pin5(PCH_pin3[6]),
    .pin6(PCH_pin3[7]), .pin7(PCL_pin7), .pin15(PCH_pin2), .pin14(PCL_pin14[0]), .pin13(PCL_pin14[1]),
    .pin12(PCL_pin14[2]), .pin11(PCL_pin14[3]), .pin10(PCL_pin10), .pin9(PCL_pin9));
  not not_3 (not_3_out, LDST);
  and and_1 (and_1_out, CLK, not_3_out, ST);
  and and_2 (and_2_out, FD, CLK);
  Hex_Digit_Display hex_digit_display_1 (.value(AOUT));  // open: dp
  Hex_Digit_Display hex_digit_display_2 (.value({pull_resistor_1_node[3], in_2[2:0]}));  // open: dp
  RAM #(.trigger("falling"), .\type ("nonvolatile")) FRAM (
    .addr(ADDRESS), .we(and_1_out), .oe(and_2_out), .clk(CLK));  // open: din, dout
  Hex_Digit_Display hex_digit_display_3 (.value(BOUT));  // open: dp
  Hex_Digit_Display hex_digit_display_4 (.value({3'b101, in_2[3]}));  // open: dp
  Pull_Resistor pull_resistor_1 (.node(pull_resistor_1_node[3]));
  assign ADDRESS = not_4_out ? {PCH_pin14, PCL_pin14} : 8'bz;  // Controlled_Buffer controlled_buffer_1
  not not_4 (not_4_out, not_5_out);
  assign ADDRESS = not_5_out ? {undriven, BOUT} : 8'bz;  // Controlled_Buffer controlled_buffer_2
  not not_5 (not_5_out, LDST);
  Hex_Digit_Display hex_digit_display_5 (.value(ADDRESS[7:4]));  // open: dp
  Hex_Digit_Display hex_digit_display_6 (.value(ADDRESS[3:0]));  // open: dp
  Hex_Digit_Display hex_digit_display_7 (.value(DATA));  // open: dp
  Pull_Resistor pull_resistor_2 (.node(ADDRESS));
  _74161 #(.ShowInternalStructure("true")) u_A (
    .pin1(nRESET), .pin2(nCLK), .pin3(DATA[0]), .pin4(DATA[1]), .pin5(DATA[2]), .pin6(DATA[3]),
    .pin7(A_pin7), .pin14(AOUT[0]), .pin13(AOUT[1]), .pin12(AOUT[2]), .pin11(AOUT[3]), .pin10(A_pin10),
    .pin9(A_pin9));  // open: pin15
  or or_1 (A_pin9, in_2[3], and_3_out);
  and and_3 (and_3_out, LDI, LDST, PT);
  assign controlled_buffer_3_out = not_6_out ? DATA : 4'bz;  // Controlled_Buffer controlled_buffer_3
  not not_6 (not_6_out, in_2[3]);
  assign controlled_buffer_3_out = in_2[3] ? BOUT : 4'bz;  // Controlled_Buffer controlled_buffer_4
  assign DATA = PT ? in_2[7:4] : 4'bz;  // Controlled_Buffer controlled_buffer_5
  // NOT_Gate not_7 has open pins: in=and_6_out, out=open
  not not_8 (not_8_out, PT);
  and and_4 (and_4_out, not_8_out, in_2[3]);
  and and_5 (and_5_out, not_8_out, A);
  and and_6 (and_6_out, ST, nand_1_out);
  nand nand_1 (nand_1_out, ADD, instNAND);
  _74161 #(.ShowInternalStructure("true")) B (
    .pin1(nRESET), .pin2(nCLK), .pin3(DATA[0]), .pin4(DATA[1]), .pin5(DATA[2]), .pin6(DATA[3]),
    .pin7(B_pin7), .pin14(BOUT[0]), .pin13(BOUT[1]), .pin12(BOUT[2]), .pin11(BOUT[3]), .pin10(B_pin10),
    .pin9(B_pin9));  // open: pin15
  and and_7 (and_7_out, LDI, PT);
  or or_2 (B_pin9, and_7_out, A);
  D_Flip_Flop C (.D(adder_1_cout), .clk(ADD), .Q(C_q));  // open: Qn, preset, reset
  assign DATA = and_4_out ? AOUT : 4'bz;  // Controlled_Buffer controlled_buffer_6
  assign DATA = and_5_out ? BOUT : 4'bz;  // Controlled_Buffer controlled_buffer_7
  assign controlled_buffer_8_out = and_6_out ? TEMPOUT : 4'bz;  // Controlled_Buffer controlled_buffer_8
  Adder #(.width(4)) adder_1 (.a(controlled_buffer_3_out), .b(AOUT), .out(adder_1_out), .cin(C_q), .cout(adder_1_cout));
  assign controlled_buffer_9_out = not_6_out ? AOUT : 4'bz;  // Controlled_Buffer controlled_buffer_9
  assign controlled_buffer_10_out = instNAND ? adder_1_out : 4'bz;  // Controlled_Buffer controlled_buffer_10
  not not_9 (not_9_out, instNAND);
  assign nand_2_out = ~(AOUT & controlled_buffer_9_out);  // NAND_Gate nand_2, 4 bits wide
  assign controlled_buffer_10_out = not_9_out ? nand_2_out : 4'bz;  // Controlled_Buffer controlled_buffer_11
  _74161 #(.ShowInternalStructure("true")) TEMP (
    .pin1(TEMP_pin1), .pin2(nCLK), .pin3(controlled_buffer_10_out[0]), .pin4(controlled_buffer_10_out[1]),
    .pin5(controlled_buffer_10_out[2]), .pin6(controlled_buffer_10_out[3]), .pin7(TEMP_pin7),
    .pin14(TEMPOUT[0]), .pin13(TEMPOUT[1]), .pin12(TEMPOUT[2]), .pin11(TEMPOUT[3]), .pin10(TEMP_pin10),
    .pin9(TEMP_pin9));  // open: pin15
  and and_8 (TEMP_pin9, ADD, instNAND);
  _74138 #(.ShowInternalStructure("true")) u_74138_1 (
    .pin1(in_2[0]), .pin2(in_2[1]), .pin3(in_2[2]), .pin4(n74138_1_pin4), .pin5(n74138_1_pin5),
    .pin6(n74138_1_pin6), .pin7(JPC), .pin15(LDI), .pin14(PT), .pin13(ADD), .pin12(instNAND), .pin11(LDST),
    .pin10(CMP), .pin9(JPZ));
  _7414 #(.ShowInternalStructure("true")) u_7414_1 (
    .pin13(in_2[3]), .pin12(A));  // open: pin1, pin2, pin3, pin4, pin5, pin6, pin11, pin10, pin9, pin8
  _7400 #(.ShowInternalStructure("true")) u_7400_1 ();  // open: pin1, pin2, pin3, pin4, pin5, pin6, pin13, pin12, pin11, pin10, pin9, pin8
  // also tied to GND on the sheet: {A_pin7, A_pin10, B_pin7, B_pin10, TEMP_pin7, n74138_1_pin4, n74138_1_pin5, TEMP_pin10}
  // also tied to VCC on the sheet: {PCH_pin7, PCL_pin7, PCH_pin10, PCH_pin9, PCL_pin10, PCL_pin9, TEMP_pin1, n74138_1_pin6}

  // Other names for the same wires on the sheet: DATAEXT[7:0] = in_2; INST[2:0] = in_2[2:0]; B = in_2[3];
  //   nA = in_2[3]; nB = A; RESET = in_1

  // Notes on the sheet:
  //   Registers
endmodule
