// Logisim project BeFour.circ as structural Verilog: 1 circuit, main circuit main
module main (
);

  wire A_pin7, A_pin10, AB, ADD, ADDRESSING, Addressing_t, ALUOP, and_1_out, and_3_out, and_4_out, and_7_out,
       B_pin7, B_pin10, CIN, CLK, CMP, COUT, INCPC, INST_pin1, INST_pin11, instNAND, JP, JPC, LD, LDI,
       LDINST, n74138_1_pin3, n74138_1_pin5, n74138_1_pin6, n74138_2_pin4, n74138_2_pin5, n74138_2_pin6,
       n74161_1_pin7, n74161_1_pin9, n74161_1_pin10, n74161_1_pin13, n74161_1_pin14, nAB, nand_1_out, nCLK,
       not_1_out, not_2_out, not_5_out, not_6_out, not_7_out, not_8_out, not_9_out, not_10_out, not_11_out,
       not_12_out, not_13_out, not_14_out, not_15_out, not_18_out, not_19_out, not_20_out, not_21_out,
       nRESET, OP1, OP2, OPERATION, or_1_out, or_2_out, or_3_out, or_4_out, or_5_out, or_7_out, or_9_out,
       or_11_out, or_12_out, or_16_out, outputA, outputB, outputLiveImm, outputTemp, PCH_pin10, PCL_pin10,
       PCL_pin15, PerformJump, RESET, ST, TEMP_pin7, TEMP_pin10, wrA, wrB;
  wire [2:0] INST;
  wire [3:0] adder_1_out, AOUT, BOUT, controlled_buffer_9_out, DATABUS, LiveImmediate, nand_2_out, PCH_pin14,
       PCL_pin14, StoredImmediate, TEMPIN, TEMPOUT;
  wire [7:0] ADDRESS, DATA;
  wire [7:4] buffer_1_out;

  or or_1 (or_1_out, OP2, PerformJump);
  not not_1 (not_1_out, or_1_out);
  or or_2 (or_2_out, PCL_pin15, not_1_out);
  or or_3 (or_3_out, PerformJump, nAB);
  and and_1 (and_1_out, INCPC, OP2);
  Clock clock_1 (.out(CLK));
  not not_2 (not_2_out, and_1_out);
  or or_4 (or_4_out, PerformJump, AB);
  POR #(.PorHighDuration(1)) por_1 (.out(RESET));
  not not_3 (nCLK, CLK);
  _74161 #(.ShowInternalStructure("true")) PCH (
    .pin1(nRESET), .pin2(or_2_out), .pin3(StoredImmediate[0]), .pin4(StoredImmediate[1]),
    .pin5(StoredImmediate[2]), .pin6(StoredImmediate[3]), .pin7(PerformJump), .pin14(PCH_pin14[0]),
    .pin13(PCH_pin14[1]), .pin12(PCH_pin14[2]), .pin11(PCH_pin14[3]), .pin10(PCH_pin10), .pin9(or_3_out));  // open: pin15
  _74161 #(.ShowInternalStructure("true")) PCL (
    .pin1(or_3_out), .pin2(not_2_out), .pin3(StoredImmediate[0]), .pin4(StoredImmediate[1]),
    .pin5(StoredImmediate[2]), .pin6(StoredImmediate[3]), .pin7(PerformJump), .pin15(PCL_pin15),
    .pin14(PCL_pin14[0]), .pin13(PCL_pin14[1]), .pin12(PCL_pin14[2]), .pin11(PCL_pin14[3]),
    .pin10(PCL_pin10), .pin9(or_4_out));
  not not_4 (nRESET, RESET);
  assign ADDRESS = not_5_out ? {PCH_pin14, PCL_pin14} : 8'bz;  // Controlled_Buffer controlled_buffer_1
  not not_5 (not_5_out, not_6_out);
  not not_6 (not_6_out, Addressing_t);
  assign ADDRESS = not_7_out ? {4'b1111, StoredImmediate} : 8'bz;  // Controlled_Buffer controlled_buffer_2
  not not_7 (not_7_out, Addressing_t);
  Hex_Digit_Display #(.decimalPoint("false")) hex_digit_display_1 (.value(AOUT));
  Hex_Digit_Display #(.decimalPoint("false")) hex_digit_display_2 (.value(BOUT));
  Hex_Digit_Display #(.decimalPoint("false")) hex_digit_display_3 (.value(DATABUS));
  Hex_Digit_Display #(.decimalPoint("false")) hex_digit_display_4 (.value({3'b101, AB}));
  _74161 #(.ShowInternalStructure("true")) u_74161_1 (
    .pin1(nRESET), .pin2(nCLK), .pin7(n74161_1_pin7), .pin14(n74161_1_pin14), .pin13(n74161_1_pin13),
    .pin10(n74161_1_pin10), .pin9(n74161_1_pin9));  // open: pin3, pin4, pin5, pin6, pin15, pin12, pin11
  Hex_Digit_Display #(.decimalPoint("false")) hex_digit_display_5 (.value(ADDRESS[7:4]));
  Hex_Digit_Display #(.decimalPoint("false")) hex_digit_display_6 (.value(ADDRESS[3:0]));
  Hex_Digit_Display #(.decimalPoint("false")) hex_digit_display_7 (.value({1'b0, INST}));
  Hex_Digit_Display #(.decimalPoint("false")) hex_digit_display_8 (.value(TEMPOUT));
  _74138 #(.ShowInternalStructure("true")) u_74138_1 (
    .pin1(n74161_1_pin14), .pin2(n74161_1_pin13), .pin3(n74138_1_pin3), .pin4(RESET), .pin5(n74138_1_pin5),
    .pin6(n74138_1_pin6), .pin15(LDINST), .pin14(OP1), .pin13(OP2), .pin12(INCPC));  // open: pin7, pin11, pin10, pin9
  not not_8 (not_8_out, outputLiveImm);
  assign DATABUS = not_8_out ? LiveImmediate : 4'bz;  // Controlled_Buffer controlled_buffer_3
  or or_5 (or_5_out, ST, OPERATION);
  not not_9 (not_9_out, INST[1]);
  and and_2 (OPERATION, OP1, OP2);
  assign DATABUS = not_10_out ? StoredImmediate : 4'bz;  // Controlled_Buffer controlled_buffer_4
  not not_10 (not_10_out, nand_1_out);
  nand nand_1 (nand_1_out, outputLiveImm, outputB, outputA, outputTemp);
  not not_11 (not_11_out, outputB);
  assign DATABUS = not_11_out ? BOUT : 4'bz;  // Controlled_Buffer controlled_buffer_5
  not not_12 (not_12_out, outputA);
  assign DATABUS = not_12_out ? AOUT : 4'bz;  // Controlled_Buffer controlled_buffer_6
  not not_13 (not_13_out, outputTemp);
  assign DATABUS = not_13_out ? TEMPOUT : 4'bz;  // Controlled_Buffer controlled_buffer_7
  not not_14 (not_14_out, or_5_out);
  and and_3 (and_3_out, AB, not_9_out);
  // Probe on DATABUS
  RAM #(.asyncread("true"), .databus("bidir"), .\type ("nonvolatile")) ram_1 (
    .addr(ADDRESS), .we(not_14_out), .oe(or_5_out), .clk(nCLK), .data(DATA));
  _74161 #(.ShowInternalStructure("true")) A (
    .pin1(nRESET), .pin2(CLK), .pin3(DATABUS[0]), .pin4(DATABUS[1]), .pin5(DATABUS[2]), .pin6(DATABUS[3]),
    .pin7(A_pin7), .pin14(AOUT[0]), .pin13(AOUT[1]), .pin12(AOUT[2]), .pin11(AOUT[3]), .pin10(A_pin10),
    .pin9(wrA));  // open: pin15
  or or_6 (wrA, INST[2], and_3_out, OP2);
  // Probe on DATA
  and and_4 (and_4_out, LDI, LD);
  assign {buffer_1_out, LiveImmediate} = DATA;  // Buffer buffer_1, 8 bits wide
  assign DATA[3:0] = not_15_out ? DATABUS : 4'bz;  // Controlled_Buffer controlled_buffer_8
  Pull_Resistor pull_resistor_1 (.node(DATA[7:4]));
  not not_15 (not_15_out, or_7_out);
  or or_7 (or_7_out, ST, OPERATION);
  _74161 #(.ShowInternalStructure("true")) B (
    .pin1(nRESET), .pin2(CLK), .pin3(DATABUS[0]), .pin4(DATABUS[1]), .pin5(DATABUS[2]), .pin6(DATABUS[3]),
    .pin7(B_pin7), .pin14(BOUT[0]), .pin13(BOUT[1]), .pin12(BOUT[2]), .pin11(BOUT[3]), .pin10(B_pin10),
    .pin9(wrB));  // open: pin15
  or or_8 (wrB, OP2, or_9_out);
  or or_9 (or_9_out, and_4_out, nAB);
  Pull_Resistor pull_resistor_2 (.node(buffer_1_out));
  _74377 #(.ShowInternalStructure("true")) u_INST (
    .pin1(INST_pin1), .pin2(INST[0]), .pin3(LiveImmediate[0]), .pin4(LiveImmediate[1]), .pin5(INST[1]),
    .pin6(INST[2]), .pin7(LiveImmediate[2]), .pin8(LiveImmediate[3]), .pin9(AB), .pin19(StoredImmediate[3]),
    .pin18(buffer_1_out[7]), .pin17(buffer_1_out[6]), .pin16(StoredImmediate[2]), .pin15(StoredImmediate[1]),
    .pin14(buffer_1_out[5]), .pin13(buffer_1_out[4]), .pin12(StoredImmediate[0]), .pin11(INST_pin11));
  not not_16 (INST_pin11, LDINST);
  or or_10 (outputA, ST, AB, OPERATION);
  // Probe on outputA
  or or_11 (or_11_out, ST, nAB, OPERATION);
  or or_12 (or_12_out, ALUOP, nAB, OP1);
  or or_13 (outputTemp, ALUOP, OP2);
  or or_14 (Addressing_t, ADDRESSING, OPERATION);
  or or_15 (outputLiveImm, LD, OPERATION);
  and and_5 (outputB, or_11_out, or_12_out);
  // Probe on outputB
  _74138 #(.ShowInternalStructure("true")) u_74138_2 (
    .pin1(INST[0]), .pin2(INST[1]), .pin3(INST[2]), .pin4(n74138_2_pin4), .pin5(n74138_2_pin5),
    .pin6(n74138_2_pin6), .pin7(JPC), .pin15(LDI), .pin14(LD), .pin13(ADD), .pin12(instNAND), .pin11(CMP),
    .pin10(ST), .pin9(JP));
  not not_17 (nAB, AB);
  and and_6 (ALUOP, ADD, instNAND);
  Adder #(.width(4)) adder_1 (.a(DATABUS), .b(AOUT), .out(adder_1_out), .cin(CIN), .cout(COUT));
  or or_16 (or_16_out, ADD, CMP);
  not not_18 (not_18_out, ALUOP);
  not not_19 (not_19_out, ADD);
  assign controlled_buffer_9_out = not_19_out ? adder_1_out : 4'bz;  // Controlled_Buffer controlled_buffer_9
  not not_20 (not_20_out, ADD);
  not not_21 (not_21_out, not_20_out);
  assign nand_2_out = ~(AOUT & DATABUS);  // NAND_Gate nand_2, 4 bits wide
  assign controlled_buffer_9_out = not_21_out ? nand_2_out : 4'bz;  // Controlled_Buffer controlled_buffer_10
  buf and_7 (and_7_out, JP);  // AND_Gate
  D_Flip_Flop C (.D(COUT), .clk(or_16_out), .Q(CIN));  // open: Qn, preset, reset
  and and_8 (ADDRESSING, LD, ST);
  assign TEMPIN = not_18_out ? controlled_buffer_9_out : 4'bz;  // Controlled_Buffer controlled_buffer_11
  or or_17 (PerformJump, and_7_out, OPERATION);
  _74161 #(.ShowInternalStructure("true")) TEMP (
    .pin1(nRESET), .pin2(OP1), .pin3(TEMPIN[0]), .pin4(TEMPIN[1]), .pin5(TEMPIN[2]), .pin6(TEMPIN[3]),
    .pin7(TEMP_pin7), .pin14(TEMPOUT[0]), .pin13(TEMPOUT[1]), .pin12(TEMPOUT[2]), .pin11(TEMPOUT[3]),
    .pin10(TEMP_pin10), .pin9(ALUOP));  // open: pin15
  Pull_Resistor pull_resistor_3 (.node(TEMPIN));
  // also tied to GND on the sheet: {n74138_1_pin3, n74138_1_pin5, A_pin7, A_pin10, B_pin7, B_pin10, INST_pin1, n74138_2_pin4, n74138_2_pin5, TEMP_pin7, TEMP_pin10}
  // also tied to VCC on the sheet: {PCL_pin10, PCH_pin10, n74161_1_pin7, n74161_1_pin10, n74161_1_pin9, n74138_1_pin6, n74138_2_pin6}

  // Other names for the same wires on the sheet: StoredInstruction[7:0] = {StoredImmediate, AB, INST}

  // Notes on the sheet:
  //   Registers
endmodule
